// Logisim project nedonand.circ as structural Verilog: 5 circuits, main circuit main
module main (
);

  dtrig dtrig_1 ();  // open: D, C, Q, nQ
  mux8 mux8_1 ();  // open: A0, A1, A2, D0, D1, D2, D3, D4, D5, D6, D7, OUT
endmodule

module dtrig (
  input  D,
  input  C,
  output Q,
  output nQ
);

  wire nand_1_out, nand_2_out;

  nand nand_1 (nand_1_out, D, C);
  nand nand_2 (nand_2_out, nand_1_out, C);
  nand nand_3 (Q, nQ, nand_1_out);
  nand nand_4 (nQ, Q, nand_2_out);
endmodule

module mux8 (
  input  A0,
  input  A1,
  input  A2,
  input  D0,
  input  D1,
  input  D2,
  input  D3,
  input  D4,
  input  D5,
  input  D6,
  input  D7,
  output OUT
);

  wire nand_1_out, nand_2_out, nand_3_out, nand_4_out, nand_5_out, nand_6_out, nand_7_out, nand_8_out,
       nand_9_out, nand_10_out, nand_11_out, nand_12_out, nand_13_out, nand_14_out, nand_15_out, nand_16_out,
       nand_17_out, nand_18_out, nand_19_out, nand_20_out, nand_21_out, nand_22_out, nand_23_out;

  nand nand_1 (nand_1_out, A0, A0);
  nand nand_2 (nand_2_out, nand_1_out, D0);
  nand nand_3 (nand_3_out, A0, D1);
  nand nand_4 (nand_4_out, nand_1_out, D2);
  nand nand_5 (nand_5_out, A0, D3);
  nand nand_6 (nand_6_out, nand_1_out, D4);
  nand nand_7 (nand_7_out, A0, D5);
  nand nand_8 (nand_8_out, nand_1_out, D6);
  nand nand_9 (nand_9_out, A0, D7);
  nand nand_10 (nand_10_out, nand_2_out, nand_3_out);
  nand nand_11 (nand_11_out, nand_4_out, nand_5_out);
  nand nand_12 (nand_12_out, nand_6_out, nand_7_out);
  nand nand_13 (nand_13_out, nand_8_out, nand_9_out);
  nand nand_14 (nand_14_out, A1, A1);
  nand nand_15 (nand_15_out, nand_14_out, nand_10_out);
  nand nand_16 (nand_16_out, A1, nand_11_out);
  nand nand_17 (nand_17_out, nand_14_out, nand_12_out);
  nand nand_18 (nand_18_out, A1, nand_13_out);
  nand nand_19 (nand_19_out, nand_15_out, nand_16_out);
  nand nand_20 (nand_20_out, nand_17_out, nand_18_out);
  nand nand_21 (nand_21_out, A2, A2);
  nand nand_22 (nand_22_out, nand_21_out, nand_19_out);
  nand nand_23 (nand_23_out, A2, nand_20_out);
  nand nand_24 (OUT, nand_22_out, nand_23_out);
endmodule

module slice (
  input  O0,
  input  O1,
  input  O2,
  input  A,
  input  B,
  input  C,
  input  H,
  input  L,
  output COUT,
  output DOUT
);

  wire nand_1_out, nand_2_out, nand_3_out, nand_4_out, nand_5_out, nand_6_out, nand_7_out, nand_9_out,
       nand_10_out, nand_11_out, nand_12_out, nand_13_out, nand_14_out, nand_15_out, nand_16_out,
       nand_17_out, nand_18_out, nand_19_out, nand_20_out, nand_21_out, nand_22_out, nand_23_out;

  nand nand_1 (nand_1_out, A, B);
  nand nand_2 (nand_2_out, A, nand_1_out);
  nand nand_3 (nand_3_out, nand_1_out, B);
  nand nand_4 (nand_4_out, nand_2_out, nand_3_out);
  nand nand_5 (nand_5_out, nand_4_out, C);
  nand nand_6 (nand_6_out, nand_4_out, nand_5_out);
  nand nand_7 (nand_7_out, nand_5_out, C);
  nand nand_8 (COUT, nand_1_out, nand_5_out);
  nand nand_9 (nand_9_out, nand_6_out, nand_7_out);
  nand nand_10 (nand_10_out, O0, O0);
  nand nand_11 (nand_11_out, nand_10_out, H);
  nand nand_12 (nand_12_out, O0, L);
  nand nand_13 (nand_13_out, nand_10_out, nand_1_out);
  nand nand_14 (nand_14_out, O0, nand_4_out);
  nand nand_15 (nand_15_out, nand_11_out, nand_12_out);
  nand nand_16 (nand_16_out, nand_13_out, nand_14_out);
  nand nand_17 (nand_17_out, O1, O1);
  nand nand_18 (nand_18_out, nand_17_out, nand_15_out);
  nand nand_19 (nand_19_out, O1, nand_16_out);
  nand nand_20 (nand_20_out, nand_18_out, nand_19_out);
  nand nand_21 (nand_21_out, O2, O2);
  nand nand_22 (nand_22_out, nand_21_out, nand_20_out);
  nand nand_23 (nand_23_out, O2, nand_9_out);
  nand nand_24 (DOUT, nand_22_out, nand_23_out);
endmodule

module alu (
  input  O0,
  input  O1,
  input  O2,
  input  A0,
  input  A1,
  input  A2,
  input  A3,
  input  B0,
  input  B1,
  input  B2,
  input  B3,
  input  C,
  output nO0,
  output nO1,
  output nO2,
  output V_prime,
  output C_prime,
  output D0,
  output D1,
  output D2,
  output D3
);

  wire nand_2_out, nand_3_out, nand_6_out, nand_7_out, nand_8_out, nand_9_out, nand_10_out, nand_11_out,
       nand_12_out, nand_13_out, nand_14_out, nand_15_out, nand_18_out, slice_1_cout, slice_2_cout,
       slice_3_cout, slice_4_cout;

  slice slice_1 (.O0(O0), .O1(O1), .O2(O2), .A(A0), .B(B0), .C(C), .H(A1), .L(C), .COUT(slice_1_cout), .DOUT(D0));
  slice slice_2 (
    .O0(O0), .O1(O1), .O2(O2), .A(A1), .B(B1), .C(slice_1_cout), .H(A2), .L(A0), .COUT(slice_2_cout),
    .DOUT(D1));
  slice slice_3 (
    .O0(O0), .O1(O1), .O2(O2), .A(A2), .B(B2), .C(slice_2_cout), .H(A3), .L(A1), .COUT(slice_3_cout),
    .DOUT(D2));
  slice slice_4 (
    .O0(O0), .O1(O1), .O2(O2), .A(A3), .B(B3), .C(slice_3_cout), .H(C), .L(A2), .COUT(slice_4_cout), .DOUT(D3));
  nand nand_1 (nO0, O0, O0);
  nand nand_2 (nand_2_out, nO0, A0);
  nand nand_3 (nand_3_out, O0, A3);
  nand nand_4 (nO1, O1, O1);
  nand nand_5 (nO2, O2, O2);
  nand nand_6 (nand_6_out, nand_2_out, nand_3_out);
  nand nand_7 (nand_7_out, nO1, nO2);
  nand nand_8 (nand_8_out, O1, nO2);
  nand nand_9 (nand_9_out, nand_7_out, nand_7_out);
  nand nand_10 (nand_10_out, slice_3_cout, slice_4_cout);
  nand nand_11 (nand_11_out, nand_9_out, nand_6_out);
  nand nand_12 (nand_12_out, nand_7_out, slice_4_cout);
  nand nand_13 (nand_13_out, slice_3_cout, nand_10_out);
  nand nand_14 (nand_14_out, nand_10_out, slice_4_cout);
  nand nand_15 (nand_15_out, nand_11_out, nand_12_out);
  nand nand_16 (V_prime, nand_13_out, nand_14_out);
  nand nand_17 (C_prime, nand_8_out, nand_18_out);
  nand nand_18 (nand_18_out, nand_15_out, nand_15_out);
endmodule
